// Logisim project microprocessor.circ as structural Verilog: 8 circuits, main circuit CPU
module CPU (
);

  wire aritmaticlogicunit_1_c, aritmaticlogicunit_1_n, aritmaticlogicunit_1_o, aritmaticlogicunit_1_z, C,
       Clk, Decode, Execute, Fetch, INC, L_FSR, M_A, N, not_1_out, O, R_D, W_D, Z;
  wire [1:0] Inst_Code;
  wire [2:0] ALU_SEL;
  wire [3:0] Mem_Addr_Reg_q, multiplexer_1_out, multiplexer_1_out_2, PC_q;
  wire [7:0] adder_1_out, aritmaticlogicunit_1_output, multiplexer_2_out, multiplexer_3_out,
       multiplexer_4_out, R_D_Out, ram_1_data, subtractor_1_out, Val_ACC, Val_FSR, Value_Given,
       Write_Data_Reg_q;
  wire [12:0] inst, rom_1_data;

  Multiplexer #(.select(2), .width(8), .enable("false")) multiplexer_1 (
    .in1(Value_Given), .in2(Val_FSR), .out({multiplexer_1_out_2, multiplexer_1_out}), .sel(Inst_Code));  // open: in0, in3
  Register #(.width(4)) Mem_Addr_Reg (.D(multiplexer_1_out), .en(M_A), .Q(Mem_Addr_Reg_q), .clk(Clk));  // open: clr
  Register Write_Data_Reg (.D(Val_ACC), .en(W_D), .Q(Write_Data_Reg_q), .clk(Clk));  // open: clr
  Multiplexer #(.select(2), .width(8), .enable("false")) multiplexer_2 (
    .in0(Value_Given), .in1(R_D_Out), .out(multiplexer_2_out), .sel(Inst_Code));  // open: in2, in3
  AritmaticLogicUnit aritmaticlogicunit_1 (
    .Input2(multiplexer_4_out), .Input1(multiplexer_2_out), .C(aritmaticlogicunit_1_c),
    .Output(aritmaticlogicunit_1_output), .ALU_SEL(ALU_SEL), .Z(aritmaticlogicunit_1_z),
    .N(aritmaticlogicunit_1_n), .O(aritmaticlogicunit_1_o));
  Subtractor subtractor_1 (.a(Val_FSR), .b(8'h1), .out(subtractor_1_out));  // open: bin, bout
  Adder_part adder_1 (.a(8'h1), .b(Val_FSR), .out(adder_1_out));  // open: cin, cout
  not not_1 (not_1_out, R_D);
  Flag_Regs flag_regs_1 (
    .Z(aritmaticlogicunit_1_z), .C(aritmaticlogicunit_1_c), .N(aritmaticlogicunit_1_n),
    .O(aritmaticlogicunit_1_o), .Z_Out(Z), .C_Out(C), .N_Out(N), .O_Out(O), .clk(Clk), .in_6(ALU_SEL));
  RAM #(.addrWidth(4), .bus("separate")) ram_1 (
    .addr(Mem_Addr_Reg_q), .din(Write_Data_Reg_q), .data(ram_1_data), .str(not_1_out), .clk(Clk), .ld(R_D));  // open: sel, clr
  Multiplexer #(.width(8), .enable("false")) multiplexer_3 (
    .in0(subtractor_1_out), .in1(adder_1_out), .out(multiplexer_3_out), .sel(INC));
  Register Read_Data_Reg (.D(ram_1_data), .en(R_D), .Q(R_D_Out), .clk(Clk));  // open: clr
  Register Accumulator (.D(aritmaticlogicunit_1_output), .en(Execute), .Q(Val_ACC), .clk(Clk));  // open: clr
  Register FSR (.D(multiplexer_3_out), .en(L_FSR), .Q(Val_FSR), .clk(Clk));  // open: clr
  Multiplexer #(.select(2), .width(8), .enable("false")) multiplexer_4 (
    .in0(Val_ACC), .in1(Val_ACC), .in2(Val_FSR), .out(multiplexer_4_out), .sel(Inst_Code));  // open: in3
  Clock u_Clk (.out(Clk));
  Counter #(.width(4), .max('hf)) PC (.count(Fetch), .Q(PC_q), .clk(Clk));  // open: load, D, carry, clr
  Control_Unit Control_Unit (
    .W_D(W_D), .R_D(R_D), .M_A(M_A), .Fetch(Fetch), .Decode(Decode), .Execute(Execute), .Instruction(inst),
    .Clk(Clk), .ALU_SEL(ALU_SEL), .Value_Given(Value_Given), .Inst_code(Inst_Code));  // open: J_Type
  ROM #(.addrWidth(4), .dataWidth(13)) rom_1 (.addr(PC_q), .data(rom_1_data), .sel(1'b1));
  Register #(.width(13)) Instruction_Reg (.D(rom_1_data), .en(Decode), .Q(inst), .clk(Clk));  // open: clr
endmodule

// ALU
module AritmaticLogicUnit (
  input  [7:0] Input1,
  input  [7:0] Input2,
  input  [2:0] ALU_SEL,
  output Z,
  output C,
  output N,
  output O,
  output [7:0] Output
);

  wire C_Add, C_Sub, O_Add, O_Sub;
  wire [7:0] add, \and , negator_1_out, \or , shiftL, shiftR, sub;

  Negator negator_1 (.in(Input1), .out(negator_1_out));
  Adder adder_1 (.input1(Input1), .input2(Input2), .Output(add), .Carry(C_Add), .Overflow(O_Add));
  Adder adder_2 (.input1(negator_1_out), .input2(Input2), .Output(sub), .Carry(C_Sub), .Overflow(O_Sub));
  assign \and  = Input1 & Input2;  // AND_Gate and, 8 bits wide
  assign \or  = Input1 | Input2;  // OR_Gate or, 8 bits wide
  Shifter shifter_1 (.in(Input1), .\dist (3'b001), .out(shiftL));
  Shifter #(.shift("lr")) shifter_2 (.in(Input1), .\dist (3'b001), .out(shiftR));
  Multiplexer #(.enable("false")) multiplexer_1 (.in0(C_Add), .in1(C_Sub), .out(C), .sel(ALU_SEL[0]));
  Multiplexer #(.enable("false")) multiplexer_2 (.in0(O_Add), .in1(O_Sub), .out(O), .sel(ALU_SEL[0]));
  Multiplexer #(.select(3), .width(8), .enable("false")) multiplexer_3 (
    .in0(add), .in1(sub), .in2(\and ), .in3(\or ), .in4(Input1), .in5(shiftL), .in6(shiftR), .in7({8{1'b0}}),
    .out(Output), .sel(ALU_SEL));
  Flag_Control flag_control_1 (.\input (Output), .Negative(N), .Zero(Z));

  // Other names for the same wires on the sheet: ALU_SEL_t[2:0] = ALU_SEL; is_sub = ALU_SEL[0]; mov[7:0] = Input1
endmodule

module Accumulator (
  input  [7:0] Input,
  input  Clock,
  input  Exec,
  input  AscSet0,
  output [7:0] \output 
);

  Pull_Resistor pull_resistor_1 (.node(AscSet0));
  D_Flip_Flop d_ff_1 (.clk(Clock), .D(Input[7]), .Q(\output [7]), .en(Exec), .reset(AscSet0));  // open: Qn, preset
  D_Flip_Flop d_ff_2 (.clk(Clock), .D(Input[6]), .Q(\output [6]), .en(Exec), .reset(AscSet0));  // open: Qn, preset
  D_Flip_Flop d_ff_3 (.clk(Clock), .D(Input[5]), .Q(\output [5]), .en(Exec), .reset(AscSet0));  // open: Qn, preset
  D_Flip_Flop d_ff_4 (.clk(Clock), .D(Input[4]), .Q(\output [4]), .en(Exec), .reset(AscSet0));  // open: Qn, preset
  D_Flip_Flop d_ff_5 (.clk(Clock), .D(Input[3]), .Q(\output [3]), .en(Exec), .reset(AscSet0));  // open: Qn, preset
  D_Flip_Flop d_ff_6 (.clk(Clock), .D(Input[2]), .Q(\output [2]), .en(Exec), .reset(AscSet0));  // open: Qn, preset
  D_Flip_Flop d_ff_7 (.clk(Clock), .D(Input[1]), .Q(\output [1]), .en(Exec), .reset(AscSet0));  // open: Qn, preset
  D_Flip_Flop d_ff_8 (.clk(Clock), .D(Input[0]), .Q(\output [0]), .en(Exec), .reset(AscSet0));  // open: Qn, preset

  // Other names for the same wires on the sheet: in0 = Input[0]; in1 = Input[1]; in2 = Input[2]; in3 = Input[3];
  //   in4 = Input[4]; in5 = Input[5]; in6 = Input[6]; in7 = Input[7]; out0 = \output [0]; out1 = \output [1];
  //   out2 = \output [2]; out3 = \output [3]; out4 = \output [4]; out5 = \output [5]; out6 = \output [6];
  //   out7 = \output [7]
endmodule

module Control_Unit (
  input  [12:0] Instruction,
  input  Clk,
  output W_D,
  output R_D,
  output [1:0] Inst_code,
  output M_A,
  output J_Type,
  output Fetch,
  output Decode,
  output Execute,
  output [7:0] Value_Given,
  output [2:0] ALU_SEL
);

  wire Execute_out, not_1_out, not_2_out, not_3_out, not_4_out, not_5_out, not_6_out, not_7_out, not_8_out,
       not_9_out;
  wire [0:0] or_1_out;
  wire [2:0] register_1_q;

  Signal_Generator signal_generator_1 (
    .ALU_Sel(Instruction[10:8]), .Fetch(Fetch), .Decode(Decode), .Execute(Execute),
    .Inst_code(Instruction[12:11]), .W_D(W_D), .R_D(R_D), .M_A(M_A));
  Register #(.width(3)) register_1 (
    .D({Fetch, Decode, or_1_out[0]}), .en(1'b1), .Q(register_1_q), .clk(Clk));  // open: clr
  not not_1 (not_1_out, register_1_q[0]);
  not not_2 (not_2_out, register_1_q[2]);
  not not_3 (not_3_out, register_1_q[1]);
  not not_4 (not_4_out, register_1_q[0]);
  not not_5 (not_5_out, register_1_q[2]);
  and u_Execute (Execute_out, not_4_out, not_3_out, not_2_out);
  and Execute_2 (Execute, not_1_out, register_1_q[1], not_5_out);
  or or_1 (or_1_out[0], Execute_out, Execute);
  not not_6 (not_6_out, register_1_q[1]);
  not not_7 (not_7_out, register_1_q[0]);
  and u_Decode (Decode, not_7_out, not_6_out, register_1_q[2]);
  not not_8 (not_8_out, register_1_q[1]);
  not not_9 (not_9_out, register_1_q[2]);
  and u_Fetch (Fetch, register_1_q[0], not_8_out, not_9_out);

  assign ALU_SEL = Instruction[10:8];
  assign Inst_code = Instruction[12:11];
  assign Value_Given = Instruction[7:0];

  // Notes on the sheet:
  //   Fetch
  //   Decode
  //   Execute
endmodule

module Adder (
  input  [7:0] input1,
  input  [7:0] input2,
  output [7:0] Output,
  output Carry,
  output Overflow
);

  wire adder_1_cout, adder_2_cout, adder_3_cout, adder_4_cout, adder_5_cout, adder_6_cout, adder_7_cout;

  Adder_part #(.width(1)) adder_1 (.a(input1[0]), .b(input2[0]), .out(Output[0]), .cin(1'b0), .cout(adder_1_cout));
  Adder_part #(.width(1)) adder_2 (
    .a(input1[1]), .b(input2[1]), .out(Output[1]), .cin(adder_1_cout), .cout(adder_2_cout));
  Adder_part #(.width(1)) adder_3 (
    .a(input1[2]), .b(input2[2]), .out(Output[2]), .cin(adder_2_cout), .cout(adder_3_cout));
  Adder_part #(.width(1)) adder_4 (
    .a(input1[3]), .b(input2[3]), .out(Output[3]), .cin(adder_3_cout), .cout(adder_4_cout));
  Adder_part #(.width(1)) adder_5 (
    .a(input1[4]), .b(input2[4]), .out(Output[4]), .cin(adder_4_cout), .cout(adder_5_cout));
  Adder_part #(.width(1)) adder_6 (
    .a(input1[5]), .b(input2[5]), .out(Output[5]), .cin(adder_5_cout), .cout(adder_6_cout));
  Adder_part #(.width(1)) adder_7 (
    .a(input1[6]), .b(input2[6]), .out(Output[6]), .cin(adder_6_cout), .cout(adder_7_cout));
  Adder_part #(.width(1)) adder_8 (.a(input1[7]), .b(input2[7]), .out(Output[7]), .cin(adder_7_cout), .cout(Carry));
  xor xor_1 (Overflow, Carry, adder_7_cout);
endmodule

module Flag_Control (
  input  [7:0] \input ,
  output Negative,
  output Zero
);

  wire or_1_out;

  or or_1 (or_1_out, \input [0], \input [1], \input [2], \input [3], \input [4], \input [5], \input [6], \input [7]);
  not not_1 (Zero, or_1_out);

  assign Negative = \input [7];
endmodule

module Signal_Generator (
  input  [1:0] Inst_code,
  input  [2:0] ALU_Sel,
  input  Fetch,
  input  Decode,
  input  Execute,
  output W_D,
  output R_D,
  output M_A
);

  wire LOAD_out, not_1_out, not_2_out, R_Type, STORE_out;

  or u_M_A (M_A, W_D, R_D);
  and STORE (STORE_out, ALU_Sel[0], ALU_Sel[1], ALU_Sel[2]);
  not not_1 (not_1_out, ALU_Sel[1]);
  and LOAD (LOAD_out, ALU_Sel[0], not_1_out, not_2_out);
  not not_2 (not_2_out, ALU_Sel[2]);
  Decoder #(.select(2), .enable("false")) decoder_1 (.out1(R_Type), .sel(Inst_code));  // open: out0, out2, out3
  and u_W_D (W_D, R_Type, Execute, STORE_out);
  and u_R_D (R_D, R_Type, LOAD_out, Execute);

  // Notes on the sheet:
  //   0-I/1-R/2-P/3-P
endmodule

// Flags
module Flag_Regs (
  input  Z,
  input  C,
  input  N,
  input  O,
  input  clk,
  input  [2:0] in_6,
  output Z_Out,
  output C_Out,
  output N_Out,
  output O_Out
);

  wire [3:0] multiplexer_1_out;

  Multiplexer #(.select(3), .width(4), .enable("false")) multiplexer_1 (
    .in0(4'b1111), .in1(4'b1111), .in2(4'b1010), .in3(4'b1010), .in4(4'b1010), .in5(4'b1010), .in6(4'b1010),
    .in7(4'b0000), .out(multiplexer_1_out), .sel(in_6));
  Register #(.width(1)) register_1 (.D(Z), .en(multiplexer_1_out[0]), .Q(Z_Out), .clk(clk));  // open: clr
  Register #(.width(1)) register_2 (.D(C), .en(multiplexer_1_out[1]), .Q(C_Out), .clk(clk));  // open: clr
  Register #(.width(1)) register_3 (.D(N), .en(multiplexer_1_out[2]), .Q(N_Out), .clk(clk));  // open: clr
  Register #(.width(1)) register_4 (.D(O), .en(multiplexer_1_out[3]), .Q(O_Out), .clk(clk));  // open: clr
endmodule
